// Logisim project G2.circ as structural Verilog: 1 circuit, main circuit main
module main (
  input  ALUsrc,
  input  RegDst,
  input  RegWrite,
  input  in_4,
  input  Enable,
  input  Clear
);

  wire clock_1_out, clock_2_out, mips_alu_1_p3, registerfile_1_p7;
  wire [4:0] multiplexer_1_out;
  wire [31:0] adder_1_p3, bit_extender_1_out, mipsprogramrom_1_p2, multiplexer_2_out, PC_q, registerfile_1_p8;

  Register #(.width(32)) PC (.D(adder_1_p3), .en(Enable), .Q(PC_q), .clk(clock_1_out), .clr(Clear));
  Clock clock_1 (.out(clock_1_out));
  // Adder adder_1: pin names not known; wires that end beside it: PC_q, 32'h4, adder_1_p3
  // MIPSProgramROM mipsprogramrom_1: pin names not known; wires that end beside it: PC_q, mipsprogramrom_1_p2
  // PLA pla_1: pin names not known; wires that end beside it: mipsprogramrom_1_p2[31:26]
  Multiplexer #(.width(5), .enable("false")) multiplexer_1 (
    .in0(mipsprogramrom_1_p2[20:16]), .in1(mipsprogramrom_1_p2[15:11]), .out(multiplexer_1_out), .sel(RegDst));
  Clock clock_2 (.out(clock_2_out));
  // RegisterFile registerfile_1: pin names not known; wires that end beside it: clock_2_out, RegWrite, multiplexer_1_out, mipsprogramrom_1_p2[25:21], mipsprogramrom_1_p2[20:16], in_4, registerfile_1_p7, registerfile_1_p8, registerfile_1_p8
  assign bit_extender_1_out = {{16{1'b0}}, mipsprogramrom_1_p2[15:0]};  // Bit_Extender bit_extender_1
  Multiplexer #(.width(32), .enable("false")) multiplexer_2 (
    .in0(registerfile_1_p8), .in1(bit_extender_1_out), .out(multiplexer_2_out), .sel(ALUsrc));
  // MIPS_ALU mips_alu_1: pin names not known; wires that end beside it: registerfile_1_p7, multiplexer_2_out, mips_alu_1_p3
  // PLA pla_2: pin names not known; wires that end beside it: mipsprogramrom_1_p2[5:0], mips_alu_1_p3
  // MIPSProgramROM mipsprogramrom_2: pin names not known
endmodule
